// Logisim project test.circ as structural Verilog: 1 circuit, main circuit main
module main (
);

  wire and_1_out, and_2_out, and_5_out, and_6_out, and_7_out, clock_1_out, clock_2_out, clock_3_out,
       clock_5_out, clock_6_out, d_ff_1_q, demultiplexer_1_out0, demultiplexer_1_out1, demultiplexer_1_out2,
       demultiplexer_1_out3, demultiplexer_4_out8, j_k_ff_1_q, j_k_ff_3_q, not_1_out, not_2_out, not_3_out,
       not_4_out, not_5_out, not_6_out, not_7_out, not_8_out, not_9_out, not_10_out, not_11_out, not_12_out,
       or_1_out, READ_ENABLE, t_ff_1_q, t_ff_2_qn, t_ff_3_q, t_ff_3_qn, t_ff_4_q, t_ff_4_qn, t_ff_5_q,
       write_enable;
  wire [1:0] or_2_out, register_6_q_2, subtractor_2_out;
  wire [3:0] register_6_q;
  wire [3:2] register_6_q_3;
  wire [4:0] demultiplexer_2_out0, demultiplexer_2_out1, REG_PIN;
  wire [7:0] rom_1_p1, rom_1_p2, rom_1_p3, rom_1_p4;
  wire [23:0] counter_1_q, PC, register_5_q;
  wire [25:0] shifter_1_out;
  wire [31:0] adder_1_out, controlled_buffer_1_out, controlled_buffer_3_out, controlled_buffer_7_out,
       demultiplexer_3_out0, demultiplexer_3_out1, divider_1_out, multiplexer_2_out, multiplexer_3_out,
       multiplier_2_out, REG_DATA, register_1_q, register_2_q, register_3_q, register_4_q, subtractor_1_out,
       X0_q, X1_q, X2_q, X3_q;
  wire [31:24] register_5_q_2;

  T_Flip_Flop t_ff_1 (.T(clock_1_out), .clk(clock_1_out), .Q(t_ff_1_q));  // open: Qn, reset, preset
  Clock clock_1 (.out(clock_1_out));
  Demultiplexer #(.select(5)) demultiplexer_1 (
    .out0(demultiplexer_1_out0), .out1(demultiplexer_1_out1), .out2(demultiplexer_1_out2),
    .out3(demultiplexer_1_out3), .in(1'b1), .sel(demultiplexer_2_out0));  // open: out4, out5, out6, out7, out8, out9, out10, out11, out12, out13, out14, out15, out16, out17, out18, out19, out20, out21, out22, out23, out24, out25, out26, out27, out28, out29, out30, out31
  Counter #(.max('hffffff), .width(24)) counter_1 (
    .load(demultiplexer_4_out8), .clk(t_ff_1_q), .D(register_5_q), .Q(counter_1_q));  // open: clr, up, count, carry
  Clock clock_2 (.out(clock_2_out));
  Register #(.width(32)) X0 (
    .D(controlled_buffer_1_out), .en(demultiplexer_1_out0), .clk(clock_2_out), .Q(X0_q));  // open: clr
  Register #(.width(32)) X1 (
    .D(controlled_buffer_1_out), .en(demultiplexer_1_out1), .clk(clock_2_out), .Q(X1_q));  // open: clr
  Register #(.width(32)) X2 (
    .D(controlled_buffer_1_out), .en(demultiplexer_1_out2), .clk(clock_2_out), .Q(X2_q));  // open: clr
  Register #(.width(32)) X3 (
    .D(controlled_buffer_1_out), .en(demultiplexer_1_out3), .clk(clock_2_out), .Q(X3_q));  // open: clr
  Demultiplexer #(.width(5)) demultiplexer_2 (
    .out0(demultiplexer_2_out0), .out1(demultiplexer_2_out1), .in(REG_PIN), .sel(not_1_out));
  not not_1 (not_1_out, write_enable);
  // ROM #(.addrWidth(24), .line("quad")) rom_1: pin names not known; wires that end beside it: rom_1_p1, rom_1_p2, rom_1_p3, rom_1_p4
  Multiplexer #(.width(24)) multiplexer_1 (.in0(PC), .sel(1'b0));  // open: in1, out
  Multiplier #(.width(24)) multiplier_1 (.a(counter_1_q), .b(24'h4), .out(PC));  // open: cin, cout
  Multiplexer #(.select(5), .width(32)) multiplexer_2 (
    .in0(X0_q), .in1(X1_q), .in2(X2_q), .in3(X3_q), .out(multiplexer_2_out), .sel(demultiplexer_2_out1));  // open: in4, in5, in6, in7, in8, in9, in10, in11, in12, in13, in14, in15, in16, in17, in18, in19, in20, in21, in22, in23, in24, in25, in26, in27, in28, in29, in30, in31
  assign controlled_buffer_1_out = write_enable ? REG_DATA : 32'bz;  // Controlled_Buffer controlled_buffer_1
  assign REG_DATA = READ_ENABLE ? multiplexer_2_out : 32'bz;  // Controlled_Buffer controlled_buffer_2
  Clock clock_3 (.out(clock_3_out));
  T_Flip_Flop t_ff_2 (.T(clock_3_out), .clk(clock_3_out), .Qn(t_ff_2_qn));  // open: Q, reset, preset
  Register #(.width(32)) register_1 (
    .D({rom_1_p4, rom_1_p3, rom_1_p2, rom_1_p1}), .en(t_ff_2_qn), .clk(clock_3_out), .Q(register_1_q),
    .clr(demultiplexer_4_out8));
  J_K_Flip_Flop j_k_ff_1 (
    .J(t_ff_2_qn), .K(clock_3_out), .clk(clock_3_out), .Q(j_k_ff_1_q));  // open: Qn, preset, reset
  Register #(.width(32)) register_2 (
    .D(register_1_q), .en(j_k_ff_1_q), .clk(j_k_ff_1_q), .Q(register_2_q));  // open: clr
  // Probe on demultiplexer_3_out0
  // Probe on register_2_q[20:0]
  Register #(.width(32)) register_3 (
    .D(demultiplexer_3_out0), .en(and_2_out), .clk(clock_5_out), .Q(register_3_q));  // open: clr
  Register #(.width(32)) register_4 (
    .D(demultiplexer_3_out1), .en(and_6_out), .clk(clock_5_out), .Q(register_4_q));  // open: clr
  Demultiplexer #(.width(32)) demultiplexer_3 (
    .out0(demultiplexer_3_out0), .out1(demultiplexer_3_out1), .in(controlled_buffer_3_out), .sel(and_6_out));
  // Probe on controlled_buffer_3_out
  // Probe on register_2_q[25:0]
  not not_2 (not_2_out, register_2_q[24]);
  not not_3 (not_3_out, register_2_q[25]);
  not not_4 (not_4_out, register_2_q[27]);
  not not_5 (not_5_out, register_2_q[29]);
  not not_6 (not_6_out, register_2_q[30]);
  not not_7 (not_7_out, register_2_q[31]);
  not not_8 (not_8_out, register_2_q[21]);
  not not_9 (not_9_out, register_2_q[23]);
  not not_10 (not_10_out, register_2_q[24]);
  not not_11 (not_11_out, register_2_q[25]);
  not not_12 (not_12_out, register_2_q[26]);
  and and_1 (and_1_out, not_8_out, register_2_q[22], not_9_out, not_10_out, not_11_out, not_12_out, register_2_q[27], register_2_q[28], register_2_q[29], register_2_q[30], register_2_q[31]);
  Shifter #(.width(26)) shifter_1 (.in(register_2_q[25:0]), .\dist (5'b00010), .out(shifter_1_out));
  and and_2 (and_2_out, write_enable, t_ff_4_qn);
  and and_3 (write_enable, not_2_out, not_3_out, register_2_q[26], not_4_out, register_2_q[28], not_5_out, not_6_out, not_7_out);
  Clock clock_4 (.out(write_enable));
  T_Flip_Flop t_ff_3 (.T(and_1_out), .clk(write_enable), .Q(t_ff_3_q), .Qn(t_ff_3_qn));  // open: reset, preset
  and and_4 (write_enable, and_1_out, t_ff_3_qn);
  // Probe on register_4_q
  Clock clock_5 (.out(clock_5_out));
  assign controlled_buffer_3_out[23:0] = and_2_out ? shifter_1_out[23:0] : 24'bz;  // Controlled_Buffer controlled_buffer_3
  T_Flip_Flop t_ff_4 (.T(write_enable), .clk(write_enable), .Q(t_ff_4_q), .Qn(t_ff_4_qn));  // open: reset, preset
  and and_5 (and_5_out, and_1_out, t_ff_3_q);
  Controlled_Buffer #(.width(32)) controlled_buffer_4 (.out(controlled_buffer_3_out), .en(write_enable));  // open: in
  Controlled_Buffer #(.width(32)) controlled_buffer_5 (.out(controlled_buffer_3_out), .en(and_5_out));  // open: in
  // Probe on register_3_q
  Adder #(.width(32)) adder_1 (.a(register_3_q), .b(register_4_q), .out(adder_1_out));  // open: cin, cout
  Subtractor #(.width(32)) subtractor_1 (
    .a(register_3_q), .b(register_4_q), .out(subtractor_1_out));  // open: bin, bout
  Multiplier #(.width(32)) multiplier_2 (
    .a(register_3_q), .b(register_4_q), .out(multiplier_2_out));  // open: cin, cout
  Divider #(.width(32)) divider_1 (.a(register_3_q), .b(register_4_q), .out(divider_1_out));  // open: upper, rem
  assign controlled_buffer_3_out[23:0] = and_6_out ? PC : 24'bz;  // Controlled_Buffer controlled_buffer_6
  and and_6 (and_6_out, write_enable, t_ff_4_q);
  J_K_Flip_Flop j_k_ff_2 (.J(t_ff_3_q), .K(write_enable), .clk(write_enable));  // open: Q, Qn, preset, reset
  Multiplexer #(.select(2), .width(32)) multiplexer_3 (
    .in0(adder_1_out), .in1(subtractor_1_out), .in2(multiplier_2_out), .in3(divider_1_out),
    .out(multiplexer_3_out), .sel(subtractor_2_out));
  Subtractor #(.width(2)) subtractor_2 (.a(or_2_out), .b(2'b01), .out(subtractor_2_out));  // open: bin, bout
  J_K_Flip_Flop j_k_ff_3 (
    .J(t_ff_4_q), .K(write_enable), .clk(write_enable), .Q(j_k_ff_3_q));  // open: Qn, preset, reset
  Register #(.width(32)) register_5 (
    .D(controlled_buffer_7_out), .en(or_1_out), .clk(clock_5_out), .Q({register_5_q_2, register_5_q}));  // open: clr
  // Probe on controlled_buffer_7_out
  assign controlled_buffer_7_out = or_1_out ? multiplexer_3_out : 32'bz;  // Controlled_Buffer controlled_buffer_7
  or or_1 (or_1_out, or_2_out[1], or_2_out[0]);
  assign or_2_out = register_6_q_2;  // OR_Gate or_2, 2 bits wide OR_Gate
  Register register_6 (
    .D(8'h18), .en(j_k_ff_3_q), .clk(j_k_ff_3_q), .Q({register_6_q_3, register_6_q_2, register_6_q}),
    .clr(d_ff_1_q));
  T_Flip_Flop t_ff_5 (.T(j_k_ff_3_q), .clk(clock_6_out), .Q(t_ff_5_q), .reset(d_ff_1_q));  // open: Qn, preset
  Clock clock_6 (.out(clock_6_out));
  D_Flip_Flop d_ff_1 (.D(t_ff_5_q), .clk(clock_6_out), .Q(d_ff_1_q));  // open: Qn, preset, reset
  and and_7 (and_7_out, 1'b1, t_ff_5_q);
  Demultiplexer #(.select(4)) demultiplexer_4 (
    .out8(demultiplexer_4_out8), .in(and_7_out), .sel(register_6_q));  // open: out0, out1, out2, out3, out4, out5, out6, out7, out9, out10, out11, out12, out13, out14, out15
  // also tied to GND on the sheet: {controlled_buffer_3_out[24], controlled_buffer_3_out[25], controlled_buffer_3_out[26], controlled_buffer_3_out[27], controlled_buffer_3_out[28], controlled_buffer_3_out[29], controlled_buffer_3_out[30], controlled_buffer_3_out[31]}

  // Notes on the sheet:
  //   write_enable
  //   contents of rom_1 (hex, n*v repeats v):
  //   0 0 40 f8 4*0 fc ff ff 14
  //   Read_enable
endmodule
